# Fritzing sketch arduino1 (saved by Fritzing 0.9.3b)
breadboards: 1

parts:
  Part1 = Arduino Uno (Rev3)
  S1 = Pushbutton [package="[THT]"]
  R1 = Resistor [tolerance=±10% resistance=10k package=THT]
  Q1 = MOSFET-NCHANNEL [package=to220v]
  R2 = Resistor [tolerance=±5% resistance=220 package=THT]

nets:
  N1: Part1.5V, S1.Pin_3, S1.Pin_4, R2.Pin_0
  N2: Part1.GND, R1.Pin_1, Q1.S
  N3: S1.Pin_1, S1.Pin_2, R1.Pin_0, Q1.G
  N4: Q1.D, R2.Pin_1
