# Fritzing sketch arduino2 (saved by Fritzing 0.9.3b)
breadboards: 1

parts:
  Part1 = Arduino Uno (Rev3)
  S1 = Pushbutton [package="[THT]"]
  R1 = Resistor [tolerance=±5% resistance=10k package=THT]
  VCC1 = Battery block 9V
  M1 = DC Motor
  D1 = Rectifier Diode [part_number=1N4001 package="300 mil [THT]"]
  Q1 = Basic FET P-Channel [package="D2Pak [SMD]"]
  R2 = Photocell (LDR) [package=THT]
  R3 = Resistor [tolerance=±5% resistance=220 package=THT]  # not connected

nets:
  N1: Part1.A0, R2.pin_1
  N2: Part1.D9_PWM, Q1.Gate
  N3: Part1.D2, S1.Pin_1, S1.Pin_2, R1.Pin_0
  N4: Part1.5V, S1.Pin_3, S1.Pin_4
  N5: Part1.GND, R1.Pin_1, VCC1.-, M1.pin_2, D1.anode, Q1.drain, Q1.source
  N6: VCC1.+, M1.pin_1, D1.cathode, R2.pin_0
