# Fritzing sketch touchChangeColour (saved by Fritzing 0.9.3b)
breadboards: 1

parts:
  Part1 = Arduino Uno (Rev3)
  R1 = Resistor [tolerance=±5% resistance=220 package=THT]
  R2 = Resistor [tolerance=±5% resistance=220 package=THT]
  R3 = Resistor [tolerance=±5% resistance=220 package=THT]
  LED1 = RGB LED (com. cathode, rgb) [package="5 mm [THT]"]
  R4 = Photocell (LDR) [package=THT]
  R5 = Photocell (LDR) [package=THT]
  R6 = Photocell (LDR) [package=THT]
  R7 = Resistor [tolerance=±5% resistance=10k package=THT]  # not connected
  R8 = Resistor [tolerance=±5% resistance=10k package=THT]
  R9 = Resistor [tolerance=±5% resistance=10k package=THT]

nets:
  N1: Part1.A0, R6.pin_1, R9.Pin_0
  N2: Part1.A1, R5.pin_1, R8.Pin_0
  N3: Part1.A2, R4.pin_1
  N4: Part1.D9_PWM, R3.Pin_1
  N5: Part1.D10_PWM/SS, R1.Pin_1
  N6: Part1.D11_PWM/MOSI, R2.Pin_1
  N7: Part1.GND, LED1.common_cathode, R8.Pin_1, R9.Pin_1
  N8: Part1.5V, R4.pin_0, R5.pin_0, R6.pin_0
  N9: R1.Pin_0, LED1.red_anode
  N10: R2.Pin_0, LED1.green_anode
  N11: R3.Pin_0, LED1.blue_anode
