# Fritzing sketch circuit (saved by Fritzing 0.9.3b)
breadboards: 1

parts:
  Part1 = Arduino Uno (Rev3)
  C1 = Electrolytic Capacitor [capacitance=1µF package="100 mil [THT, electrolytic]"]
  C2 = Electrolytic Capacitor [capacitance=1µF package="100 mil [THT, electrolytic]"]
  U1 = POT [package=pot_alpha_rv16af-20]
  J1 = Basic Servo

nets:
  N1: Part1.A0, U1.S
  N2: Part1.D9_PWM, J1.pulse
  5V: Part1.5V, C1.+, U1.E, J1.vcc
  GND: Part1.GND, C1.-, C2.-, U1.A, J1.gnd
