# Fritzing sketch the circuit (saved by Fritzing 0.9.3b)
breadboards: 1

parts:
  Part1 = Arduino Uno (Rev3)
  J1 = Piezo Speaker
  S1 = Pushbutton [package="[THT]"]
  S2 = Pushbutton [package="[THT]"]
  S3 = Pushbutton [package="[THT]"]
  S4 = Pushbutton [package="[THT]"]
  R1 = Resistor [tolerance=±5% resistance=10k package=THT]
  R2 = Resistor [tolerance=±5% resistance=1M package=THT]
  R3 = Resistor [tolerance=±5% resistance=10k package=THT]
  R4 = Resistor [tolerance=±5% resistance=220 package=THT]

nets:
  N1: Part1.A0, S1.Pin_1, S1.Pin_2, S2.Pin_1, S2.Pin_2, S3.Pin_1, S3.Pin_2, S4.Pin_1, S4.Pin_2, R1.Pin_0
  N2: Part1.D8, J1.pin2
  N3: Part1.5V, S4.Pin_3, S4.Pin_4, R2.Pin_1, R3.Pin_1
  N4: Part1.GND, J1.pin1, R1.Pin_1
  N5: S1.Pin_3, S1.Pin_4, R2.Pin_0
  N6: S2.Pin_3, S2.Pin_4, R3.Pin_0
  N7: S3.Pin_3, S3.Pin_4, R4.Pin_0
