# Fritzing sketch assignment (saved by Fritzing 0.9.3b)
breadboards: 1

parts:
  Part1 = Arduino Uno (Rev3)
  R1 = Resistor [tolerance=±5% resistance=10k package=THT]
  R2 = Photocell (LDR) [package=THT]
  T1 = LM35 Temperature Sensor [package="TO92 [THT]"]
  RHT1 = Humidity and Temperature Sensor RHT03
  R3 = Rotary Potentiometer (Small) [maximum_resistance=100kΩ package=THT]
  Part2 = Arduino Ethernet Shield (Rev3)  # not connected

nets:
  N1: Part1.A0, T1.Vout
  N2: Part1.A1, RHT1.Data-signal
  N3: Part1.A2, R1.Pin_0, R2.pin_1
  N4: Part1.A3, R3.wiper
  5V: Part1.5V, R2.pin_0, T1.+Vs, RHT1.Vcc, R3.leg1
  GND: Part1.GND, T1.GND, RHT1.GND_2, R3.leg2
